# Fritzing sketch Circut Diagram ChemE Car EE Team 2017-2018 (saved by Fritzing 0.9.3b)

parts:
  Part1 = Arduino Prototyping Shield
  J1 = female pin header, 8 pins [form="♀ (female)"]
  J2 = female alternating pin header, 10 pins [form="♀ (female)"]
  J3 = female pin header, 6 pins [form="♀ (female)"]
  J4 = female pin header, 8 pins [form="♀ (female)"]
  J5 = female pin header, 1 pin [form="♀ (female)"]
  R1 = Resistor [tolerance=±5% resistance=100k package="0603 [SMD]"]
  C1 = Ceramic Capacitor [capacitance=1µF package="200 mil [THT, multilayer]"]
  R2 = Resistor [tolerance=±5% resistance=100k package="0603 [SMD]"]
  R3 = Resistor [tolerance=±5% resistance=100k package="0603 [SMD]"]
  R4 = Resistor [tolerance=±5% resistance=100k package="0603 [SMD]"]
  R5 = Resistor [tolerance=±5% resistance=100k package="0603 [SMD]"]
  S1 = Toggle Switch [package=THT]
  S2 = Toggle Switch [package=THT]
  S3 = Toggle Switch [package=THT]
  S4 = Toggle Switch [package=THT]
  VCC2 = Battery
  Part2 = Ambient Light Sensor (TEMT6000 Breakout Board)
  D1 = Rectifier Diode [part_number=1N4001 package="300 mil [THT]"]
  J6 = female pin header, 3 pins [form="♀ (female)"]
  U2 = DIODE-ZENER [package=diode-zener]
  J7 = female pin header, 2 pins [form="♀ (female)"]
  M1 = DC Motor
  J8 = male pin header, 2 pins [form="♂ (male)"]
  S5 = Round Pushbutton
  J9 = male pin header, 8 pins [form="♂ (male)"]
  VCC3 = Battery block 9V
  R6 = Photocell (LDR) [package=THT]
  J10 = male pin header, 5 pins [form="♂ (male)"]
  LED1 = LEDs [package=led10mm]
  LED2 = LEDs [package=led10mm]
  R7 = Resistor [tolerance=±5% resistance=100k package="0603 [SMD]"]
  R8 = Resistor [tolerance=±5% resistance=100k package="0603 [SMD]"]
  J15 = male pin header, 1 pin [form="♂ (male)"]
  J18 = female pin header, 1 pin [form="♀ (female)"]
  J19 = male pin header, 1 pin [form="♂ (male)"]
  Q1 = npn-Powertransistor [package="TO220 [THT]"]
  J16 = female pin header, 5 pins [form="♀ (female)"]
  J12 = female pin header, 5 pins [form="♀ (female)"]
  J17 = male pin header, 5 pins [form="♂ (male)"]
  J14 = male pin header, 5 pins [form="♂ (male)"]
  LED3 = LEDs [package=led10mm]
  R9 = Resistor [tolerance=±5% resistance=100k package="0603 [SMD]"]
  J21 = male pin header, 2 pins [form="♂ (male)"]

nets:
  N1: Part1.A0, Part1.N$76, Part1.N$118, J3.pin1, J5.pin1, R1.Pin_0, C1.0, R6.pin_1, J15.pin1
  N2: Part1.A1, J3.pin2
  N3: Part1.A2, J3.pin3
  N4: Part1.A3, J3.pin4
  N5: Part1.A4, J3.pin5
  N6: Part1.A5, J3.pin6
  +5V: Part1.+5V, J4.pin5, S3.L1, S4.L1, Part2.VCC, S5.leg0, J10.pin4, J12.pin1, J12.pin2, J12.pin3, J12.pin4, J12.pin5, J14.pin1, J14.pin2, J14.pin3, J14.pin4, J14.pin5, LED3.C
  N7: Part1.D0(RX), J1.pin8, J9.pin8
  N8: Part1.D1(TX), J1.pin7, J9.pin7
  N9: Part1.D2, J1.pin6, R2.Pin_0, S5.leg1, J9.pin6
  N10: Part1.D3, J1.pin5, R3.Pin_0, S4.COM, J9.pin5
  N11: Part1.D4, J1.pin4, R4.Pin_0, S3.COM, J9.pin4
  N12: Part1.D5, J1.pin3, R5.Pin_0, Part2.S, J9.pin3
  N13: Part1.D6, Part1.N$87, J1.pin2, J6.pin3, J9.pin2, LED1.C, Q1.base
  N14: Part1.D7, J1.pin1, J9.pin1, LED2.C
  N15: Part1.IOREF, J4.pin1, J4.pin2
  N16: Part1.RESET, J4.pin3
  N17: Part1.3.3V, J4.pin4, R6.pin_0, J10.pin5
  GND: Part1.GND, Part1.N$85, Part1.N$86, Part1.N$178, Part1.N$406, Part1.N$407, Part1.N$409, Part1.N$412, J2.pin4, J4.pin6, J4.pin7, R1.Pin_1, C1.1, R2.Pin_1, R3.Pin_1, R4.Pin_1, R5.Pin_1, VCC2.-, Part2.GND, D1.anode, J6.pin1, VCC3.-, J10.pin2, J10.pin3, R7.Pin_1, R8.Pin_1, Q1.emitter, J16.pin1, J16.pin2, J16.pin3, J16.pin4, J16.pin5, J17.pin1, J17.pin2, J17.pin3, J17.pin4, J17.pin5, R9.Pin_1
  N18: Part1.+9V, J4.pin8, S2.COM, J10.pin1
  N19: Part1.D8, J2.pin10
  N20: Part1.D10, J2.pin8
  N21: Part1.D11, J2.pin7
  N22: Part1.D12, J2.pin6
  N23: Part1.D13, J2.pin5
  N24: Part1.AREF, J2.pin3
  N25: Part1.SDA, J2.pin2
  N26: Part1.SCL, J2.pin1
  N27: Part1.N$50, J21.pin1
  N28: Part1.N$51, J21.pin2
  N29: Part1.N$54, Part1.N$55, S1.COM, U2.C, J7.pin1, J7.pin2, M1.pin_1, J8.pin1, J8.pin2
  N30: Part1.N$65, Part1.N$66, Part1.N$67, Part1.N$74, Part1.N$84, Part1.N$90, D1.cathode, J6.pin2, U2.A, M1.pin_2, J18.pin1, J19.pin1, Q1.collector
  N31: S1.L1, VCC2.+
  N32: S2.L1, VCC3.+
  N33: LED1.A, R7.Pin_0
  N34: LED2.A, R8.Pin_0
  N35: LED3.A, R9.Pin_0

notes:
  'Digital' Light Sensor
  ALS
  Green LED
  Blue LED
  Power to Motor (Mech Team)
  Power from battery team
  White LED for some systems
