# Fritzing sketch ambient light sensor (saved by Fritzing 0.9.1b)
breadboards: 1

parts:
  Part1 = Arduino Pro Mini v13
  Part2 = Ambient Light Sensor (TEMT6000 Breakout Board)
  VCC1 = 4 x AAA Battery Mount

nets:
  VCC: Part1.VCC, Part2.VCC, VCC1.+
  GND: Part1.GND, Part2.GND, VCC1.-
  N1: Part1.A0, Part2.S

notes:
  https://anasdalintakam.blogspot.in/

// code stored in the sketch: ambientlighsensor.ino
int temt6000Pin = A0;

void setup() {
  Serial.begin(112500);
  pinMode(3,OUTPUT);
}

void loop() {
  int light_value = analogRead(temt6000Pin);
  Serial.println(light_value);

  delay(100); 
  if (light_value>1000){digitalWrite(3,HIGH);}
  
  //only here to slow down the output so it is easier to read
}
